// Logisim project subtask_two_XXXX.circ as structural Verilog: 1 circuit, main circuit main
module main (
  input  D,
  input  C,
  input  B,
  input  A,
  output a_2,
  output b_2,
  output c_2,
  output d_2,
  output e,
  output f,
  output g
);

  wire and_1_out, and_2_out, and_3_out, and_4_out, and_5_out, and_6_out, and_7_out, and_8_out, and_9_out,
       and_10_out, and_11_out, and_12_out, and_13_out, and_14_out, and_15_out, and_16_out, not_1_out,
       not_2_out, not_3_out, not_4_out, not_5_out, not_6_out, not_7_out, not_8_out, not_9_out, not_10_out,
       not_11_out, not_12_out, not_13_out, not_14_out, not_15_out, not_16_out, not_17_out, not_18_out,
       not_19_out, not_20_out, not_21_out;

  not not_1 (not_1_out, D);
  not not_2 (not_2_out, B);
  not not_3 (not_3_out, D);
  not not_4 (not_4_out, C);
  not not_5 (not_5_out, C);
  not not_6 (not_6_out, D);
  not not_7 (not_7_out, B);
  not not_8 (not_8_out, D);
  not not_9 (not_9_out, B);
  not not_10 (not_10_out, C);
  not not_11 (not_11_out, D);
  not not_12 (not_12_out, B);
  not not_13 (not_13_out, D);
  not not_14 (not_14_out, D);
  not not_15 (not_15_out, C);
  not not_16 (not_16_out, D);
  not not_17 (not_17_out, C);
  not not_18 (not_18_out, C);
  not not_19 (not_19_out, D);
  not not_20 (not_20_out, B);
  and and_1 (and_1_out, not_1_out, not_2_out);
  and and_2 (and_2_out, D, B);
  and and_3 (and_3_out, not_3_out, not_4_out);
  or or_1 (b_2, and_3_out, not_21_out, and_4_out);
  not not_21 (not_21_out, B);
  and and_4 (and_4_out, D, C);
  or or_2 (c_2, not_5_out, B, D);
  and and_5 (and_5_out, not_6_out, not_7_out);
  and and_6 (and_6_out, not_8_out, C);
  and and_7 (and_7_out, C, not_9_out);
  and and_8 (and_8_out, D, not_10_out, B);
  and and_9 (and_9_out, not_11_out, not_12_out);
  or or_3 (e, and_9_out, and_10_out);
  and and_10 (and_10_out, not_13_out, C);
  and and_11 (and_11_out, not_14_out, not_15_out);
  and and_12 (and_12_out, not_16_out, B);
  and and_13 (and_13_out, not_17_out, B);
  and and_14 (and_14_out, not_18_out, B);
  and and_15 (and_15_out, not_19_out, C);
  and and_16 (and_16_out, C, not_20_out);
  or or_4 (a_2, and_1_out, A, C, and_2_out);
  or or_5 (d_2, and_5_out, A, and_6_out, and_7_out, and_8_out);
  or or_6 (f, and_11_out, A, and_12_out, and_13_out);
  or or_7 (g, A, and_14_out, and_15_out, and_16_out);
endmodule
